# Fritzing sketch CarLightcontrol (saved by Fritzing 0.9.10b)
perfboards: 2

parts:
  Rueckfahr_(27) = pnp-Powertransistor [package="TO220 [THT]"]
  Blink_(32) = pnp-Powertransistor [package="TO220 [THT]"]
  Brems_(33) = pnp-Powertransistor [package="TO220 [THT]"]
  Ruecklicht_(13) = pnp-Powertransistor [package="TO220 [THT]"]
  J1 = JST XH 2A male [form="♂ (male)" package=THT]  # not connected
  U1 = JST-XH-6A  # not connected
  U2 = POT [knob_status=50% power=0.5W package=pot_mammoth]  # not connected
  U3 = POT [knob_status=50% power=0.5W package=pot_mammoth]  # not connected
  U4 = POT [knob_status=50% power=0.5W package=pot_mammoth]  # not connected
  U5 = POT [knob_status=50% power=0.5W package=pot_mammoth]  # not connected
  Q1 = TRANSISTOR_NPN [package=to-92-ammo]
  Ruecklicht_(15) = JST XH 3A Male [chip_label=? package=THT]  # not connected
  Rueckfahr_(17) = JST XH 3A Male [chip_label=? package=THT]  # not connected
  Brems_(21) = JST XH 3A Male [chip_label=? package=THT]  # not connected
  Blink_(23) = JST XH 3A Male [chip_label=? package=THT]  # not connected
  J2 = rounded female pin header, 15 pins [form="♀ (female rounded)"]  # not connected
  J3 = rounded female pin header, 15 pins [form="♀ (female rounded)"]  # not connected
  R4 = Resistor upright [tolerance=±5% resistance=2200 package=THT]
  Q2 = TRANSISTOR_NPN [package=to-92-ammo]
  R6 = Resistor upright [tolerance=±5% resistance=2200 package=THT]
  Q3 = TRANSISTOR_NPN [package=to-92-ammo]
  R8 = Resistor upright [tolerance=±5% resistance=2200 package=THT]
  Q4 = TRANSISTOR_NPN [package=to-92-ammo]
  R10 = Resistor upright [tolerance=±5% resistance=2200 package=THT]
  R11 = Resistor upright [tolerance=±5% resistance=2200 package=THT]
  R12 = Resistor upright [tolerance=±5% resistance=2200 package=THT]
  R13 = Resistor upright [tolerance=±5% resistance=2200 package=THT]
  R14 = Resistor upright [tolerance=±5% resistance=2200 package=THT]
  J4 = rounded female pin header, 3 pins [form="♀ (female rounded)"]
  J5 = rounded female pin header, 3 pins [form="♀ (female rounded)"]
  J6 = rounded female pin header, 3 pins [form="♀ (female rounded)"]
  J7 = rounded female pin header, 3 pins [form="♀ (female rounded)"]
  J8 = rounded female pin header, 3 pins [form="♀ (female rounded)"]
  J9 = rounded female pin header, 3 pins [form="♀ (female rounded)"]
  J10 = rounded female pin header, 3 pins [form="♀ (female rounded)"]
  J11 = rounded female pin header, 3 pins [form="♀ (female rounded)"]
  J12 = rounded female pin header, 1 pin [form="♀ (female rounded)"]
  J13 = rounded female pin header, 1 pin [form="♀ (female rounded)"]
  J14 = rounded female pin header, 1 pin [form="♀ (female rounded)"]
  J15 = rounded female pin header, 1 pin [form="♀ (female rounded)"]
  J16 = rounded female pin header, 1 pin [form="♀ (female rounded)"]
  J17 = rounded female pin header, 1 pin [form="♀ (female rounded)"]
  J18 = rounded female pin header, 1 pin [form="♀ (female rounded)"]
  J19 = rounded female pin header, 1 pin [form="♀ (female rounded)"]
  J20 = rounded female pin header, 2 pins [form="♀ (female rounded)"]
  J21 = rounded female pin header, 6 pins [form="♀ (female rounded)"]
  J22 = rounded female pin header, 15 pins [form="♀ (female rounded)"]
  J23 = rounded female pin header, 15 pins [form="♀ (female rounded)"]
  J24 = rounded female pin header, 3 pins [form="♀ (female rounded)"]
  J25 = rounded female pin header, 3 pins [form="♀ (female rounded)"]
  J26 = rounded female pin header, 3 pins [form="♀ (female rounded)"]
  J27 = rounded female pin header, 3 pins [form="♀ (female rounded)"]
  J28 = rounded female pin header, 2 pins [form="♀ (female rounded)"]
  J29 = rounded female pin header, 2 pins [form="♀ (female rounded)"]  # not connected
  J31 = rounded female pin header, 2 pins [form="♀ (female rounded)"]  # not connected
  J32 = rounded female pin header, 2 pins [form="♀ (female rounded)"]
  MP1584EN_Board1 = MP1584EN Power Regulator Board [part_number=MP1584EN]  # not connected

nets:
  N1: Rueckfahr_(27).base, R6.Pin_1
  N2: Blink_(32).base, R10.Pin_1
  N3: Brems_(33).base, R8.Pin_1
  N4: Ruecklicht_(13).base, R4.Pin_1
  N5: Q1.B, R11.Pin_1
  N6: Q2.B, R12.Pin_1
  N7: Q3.B, R13.Pin_1
  N8: Q4.B, R14.Pin_1
  N9: J4.pin3, J14.pin1
  N10: J5.pin3, J12.pin1
  N11: J6.pin3, J13.pin1
  N12: J7.pin3, J15.pin1
  N13: J8.pin2, J21.pin1
  N14: J9.pin2, J21.pin2
  N15: J10.pin2, J21.pin4
  N16: J11.pin2, J21.pin5
  N17: J16.pin1, J22.pin6
  N18: J17.pin1, J22.pin7
  N19: J18.pin1, J22.pin10
  N20: J19.pin1, J22.pin13
  N21: J20.pin1, J28.pin2
  N22: J22.pin15, J32.pin1
  N23: J23.pin1, J24.pin1
  N24: J23.pin5, J25.pin1
  N25: J23.pin9, J26.pin1
  N26: J23.pin13, J27.pin1
  N27: J23.pin15, J27.pin3

notes:
  - Potentiometer analog pollen (dann kann man das auch mit dem Website-Dimming verheiraten)
  - Blinklicht-Frequenz einstellbar auf Website (TODO PWM UND Blinken)

custom parts:
  JST XH 2A male: JST XH-2A
  JST-XH-6A: JST XH 6A (2.54)
  JST XH 3A Male: 2.54 Mm JST "XH" connector
  Resistor upright: A generic upright standing resistor (0.25W)
  MP1584EN Power Regulator Board: The MP1584EN is a high frequency step-down switching regulator. The input voltage range is 4.5V to 28V. The output voltage is set by the board's potentiometer.
